// Logisim project HWproject.circ as structural Verilog
module _1 (
  input  c_in,
  input  a,
  input  b,
  output sum,
  output c_out
);

  wire and_1_out, and_2_out, and_3_out, and_4_out, xor_1_out;

  and and_1 (and_1_out, a, b, c_in);
  ExactlyOne xor_1 (.out(xor_1_out), .in0(c_in), .in1(a), .in4(b));
  and and_2 (and_2_out, b, c_in);
  and and_3 (and_3_out, a, c_in);
  and and_4 (and_4_out, a, b);
  xor xor_2 (sum, and_1_out, xor_1_out);
  or or_1 (c_out, and_2_out, and_3_out, and_4_out);
endmodule

module _16 (
  input  in_1,
  input  [15:0] a,
  input  [15:0] b,
  input  c_out,
  output [15:0] sum
);

  wire n4_1_c_out, n4_2_c_out, n4_3_c_out;

  _4 u_4_1 (.c_in(in_1), .a(a[3:0]), .b(b[3:0]), .sum(sum[3:0]), .c_out(n4_1_c_out));
  _4 u_4_2 (.c_in(n4_1_c_out), .a(a[7:4]), .b(b[7:4]), .sum(sum[7:4]), .c_out(n4_2_c_out));
  _4 u_4_3 (.c_in(n4_2_c_out), .a(a[11:8]), .b(b[11:8]), .sum(sum[11:8]), .c_out(n4_3_c_out));
  _4 u_4_4 (.c_in(n4_3_c_out), .a(a[15:12]), .b(b[15:12]), .sum(sum[15:12]), .c_out(c_out));
endmodule

module _2__4 (
  input  c_in,
  input  [3:0] a,
  input  [3:0] b,
  output [3:0] sum,
  output c_out
);

  wire n1_1_c_out, n1_2_c_out, n1_3_c_out;

  _1 u_1_1 (.c_in(c_in), .a(a[0]), .b(b[0]), .sum(sum[0]), .c_out(n1_1_c_out));
  _1 u_1_2 (.c_in(n1_1_c_out), .a(a[1]), .b(b[1]), .sum(sum[1]), .c_out(n1_2_c_out));
  _1 u_1_3 (.c_in(n1_2_c_out), .a(a[2]), .b(b[2]), .sum(sum[2]), .c_out(n1_3_c_out));
  _1 u_1_4 (.c_in(n1_3_c_out), .a(a[3]), .b(b[3]), .sum(sum[3]), .c_out(c_out));
endmodule

module _4 (
  input  c_in,
  input  [3:0] a,
  input  [3:0] b,
  output [3:0] sum,
  output c_out
);

  _2__4 u_2_4_1 (.c_in(c_in), .a(a), .b(b), .sum(sum), .c_out(c_out));
endmodule

module _32 (
  input  in_1,
  input  [31:0] in_2,
  input  [31:0] in_3,
  input  c_out,
  output [31:0] out_5
);

  wire n16_32_1_out_5;

  _16____32 u_16_32_1 (.in_1(in_1), .a(in_2[15:0]), .b(in_3[15:0]), .out_4(out_5[15:0]), .out_5(n16_32_1_out_5));
  _16____32 u_16_32_2 (.in_1(n16_32_1_out_5), .a(in_2[31:16]), .b(in_3[31:16]), .out_4(out_5[31:16]), .out_5(c_out));
endmodule

module _16____32 (
  input  in_1,
  input  [15:0] a,
  input  [15:0] b,
  output [15:0] out_4,
  output out_5
);

  _16 u_16_1 (.in_1(in_1), .a(a), .b(b), .sum(out_4), .c_out(out_5));
endmodule
